# Fritzing sketch ParallelFLASHDumper (saved by Fritzing 0.4.2b)
breadboards: 5

parts:
  Arduino1 = Arduino
  74LV595N_2 = 74HC595 [package="DIP16 [THT]"]
  74LV595N_1 = 74HC595 [package="DIP16 [THT]"]
  FLASH_MEMORY = IC, DIP package, 56 pins [chip_label="FLASH MEMORY" spacing=600mil]  # not connected
  HEF4104B_2 = IC, DIP package, 16 pins [chip_label=HEF4104B spacing=300mil]
  HEF4104B_1 = IC, DIP package, 16 pins [chip_label=HEF4104B spacing=300mil]
  74LV595N_3 = 74HC595 [package="DIP16 [THT]"]
  addr_J3 = female pin header, 8 pins [form="♀ (female)"]
  addr_J2 = female pin header, 8 pins [form="♀ (female)"]
  data_J2 = female pin header, 8 pins [form="♀ (female)"]
  data_J1 = female pin header, 8 pins [form="♀ (female)"]
  addr_J1 = female pin header, 8 pins [form="♀ (female)"]

nets:
  GND: Arduino1.GND, 74LV595N_2.GND, 74LV595N_2.MR, 74LV595N_2.OE, 74LV595N_1.GND, 74LV595N_1.MR, 74LV595N_1.OE, HEF4104B_2.pin8, HEF4104B_1.pin8, 74LV595N_3.GND, 74LV595N_3.MR, 74LV595N_3.OE
  N1: Arduino1.D11, HEF4104B_2.pin10, HEF4104B_1.pin10
  N2: Arduino1.D10, HEF4104B_2.pin3
  N3: Arduino1.D9, HEF4104B_2.pin9, HEF4104B_1.pin9
  N4: Arduino1.D8, 74LV595N_2.ST_CP, 74LV595N_1.ST_CP, 74LV595N_3.ST_CP
  N5: Arduino1.D7, 74LV595N_3.DS
  N6: Arduino1.D6, 74LV595N_2.SH_CP, 74LV595N_1.SH_CP, 74LV595N_3.SH_CP
  5V: Arduino1.+5V, 74LV595N_2.VCC, 74LV595N_1.VCC, HEF4104B_2.pin16, HEF4104B_1.pin16, 74LV595N_3.VCC
  N7: 74LV595N_2.Q1, addr_J2.pin2
  N8: 74LV595N_2.Q2, addr_J2.pin3
  N9: 74LV595N_2.Q3, addr_J2.pin4
  N10: 74LV595N_2.Q4, addr_J2.pin5
  N11: 74LV595N_2.Q5, addr_J2.pin6
  N12: 74LV595N_2.Q6, addr_J2.pin7
  N13: 74LV595N_2.Q7, addr_J2.pin8
  N14: 74LV595N_2.Q7', 74LV595N_1.DS
  N15: 74LV595N_2.DS, 74LV595N_3.Q7'
  N16: 74LV595N_2.Q0, addr_J2.pin1
  N17: 74LV595N_1.Q1, addr_J1.pin2
  N18: 74LV595N_1.Q2, addr_J1.pin3
  N19: 74LV595N_1.Q3, addr_J1.pin4
  N20: 74LV595N_1.Q4, addr_J1.pin5
  N21: 74LV595N_1.Q5, addr_J1.pin6
  N22: 74LV595N_1.Q6, addr_J1.pin7
  N23: 74LV595N_1.Q7, addr_J1.pin8
  N24: 74LV595N_1.Q0, addr_J1.pin1
  N25: HEF4104B_2.pin1, data_J2.pin1
  N26: HEF4104B_2.pin4, data_J2.pin5
  N27: HEF4104B_2.pin5, data_J2.pin6
  N28: HEF4104B_2.pin6, data_J2.pin7
  N29: HEF4104B_2.pin7, data_J2.pin8
  N30: HEF4104B_2.pin11, HEF4104B_1.pin3
  N31: HEF4104B_2.pin13, data_J2.pin4
  N32: HEF4104B_2.pin14, data_J2.pin3
  N33: HEF4104B_2.pin15, data_J2.pin2
  N34: HEF4104B_1.pin1, data_J1.pin1
  N35: HEF4104B_1.pin4, data_J1.pin5
  N36: HEF4104B_1.pin5, data_J1.pin6
  N37: HEF4104B_1.pin6, data_J1.pin7
  N38: HEF4104B_1.pin7, data_J1.pin8
  N39: HEF4104B_1.pin13, data_J1.pin4
  N40: HEF4104B_1.pin14, data_J1.pin3
  N41: HEF4104B_1.pin15, data_J1.pin2
  N42: 74LV595N_3.Q1, addr_J3.pin2
  N43: 74LV595N_3.Q2, addr_J3.pin3
  N44: 74LV595N_3.Q3, addr_J3.pin4
  N45: 74LV595N_3.Q4, addr_J3.pin5
  N46: 74LV595N_3.Q5, addr_J3.pin6
  N47: 74LV595N_3.Q6, addr_J3.pin7
  N48: 74LV595N_3.Q7, addr_J3.pin8
  N49: 74LV595N_3.Q0, addr_J3.pin1

notes:
  Parallel FLASH Dumper
  software and details:
  http://deadhacker.com/tools/
  * See wire names for pin order.
  * FLASH chip shown is just an example. The pinmap for your target will differ. Consult datasheet for your target.
  * Make certain the Ditial out voltage is at a voltage range the FLASH chip is compatible with.
  This breadboard is just used to show order of bits...
  (Lowest bit (A0) is on right most pin, highest on left most pin)
  Output (address) board
  Input (data) board
  NOTE: Pin map shown is for HEF4104B. You could also use: 74LS299, 74HC165 74LV166 with different pin mapping
